// Logisim project Part1.circ as structural Verilog: 6 circuits, main circuit main
module main (
  input  in_1,
  input  in_2,
  input  in_3,
  input  in_4,
  input  in_5,
  input  in_6,
  input  A,
  input  B,
  input  in_9,
  input  A_2,
  input  B_2,
  input  S0,
  input  S1,
  input  C,
  input  D,
  output out_16,
  output out_17,
  output out_18,
  output out_19,
  output out_20
);

  NAND1 nand1_1 (.In1(in_1), .In2(in_2), .Out1(out_16));
  NOR1 nor1_1 (.in_1(in_3), .in_2(in_4), .out_3(out_17));
  XOR1 xor1_1 (.in_1(in_5), .in_2(in_6), .out_3(out_18));
  Two2OneMux two2onemux_1 (.in_1(A), .S(B), .B(in_9), .out_4(out_19));
  Four2OneMux four2onemux_1 (.A(A_2), .B(B_2), .S1(S0), .S0(S1), .C(C), .D(D), .out_7(out_20));

  // Notes on the sheet:
  //   S
  //   NAND
  //   NOR
endmodule

module NAND1 (
  input  In1,
  input  In2,
  output Out1
);

  wire and_1_out;

  and and_1 (and_1_out, In1, In2);
  not not_1 (Out1, and_1_out);
endmodule

module NOR1 (
  input  in_1,
  input  in_2,
  output out_3
);

  wire or_1_out;

  or or_1 (or_1_out, in_1, in_2);
  not not_1 (out_3, or_1_out);
endmodule

module XOR1 (
  input  in_1,
  input  in_2,
  output out_3
);

  wire nand1_1_out1, or_1_out;

  or or_1 (or_1_out, in_1, in_2);
  NAND1 nand1_1 (.In1(in_1), .In2(in_2), .Out1(nand1_1_out1));
  and and_1 (out_3, or_1_out, nand1_1_out1);
endmodule

module Two2OneMux (
  input  in_1,
  input  S,
  input  B,
  output out_4
);

  wire and_1_out, and_2_out, not_1_out;

  not not_1 (not_1_out, S);
  and and_1 (and_1_out, in_1, not_1_out);
  and and_2 (and_2_out, S, B);
  or or_1 (out_4, and_1_out, and_2_out);

  // Notes on the sheet:
  //   A
endmodule

module Four2OneMux (
  input  A,
  input  B,
  input  S1,
  input  S0,
  input  C,
  input  D,
  output out_7
);

  wire two2onemux_1_out_4, two2onemux_2_out_4;

  Two2OneMux two2onemux_1 (.in_1(A), .S(S0), .B(B), .out_4(two2onemux_1_out_4));
  Two2OneMux two2onemux_2 (.in_1(C), .S(S0), .B(D), .out_4(two2onemux_2_out_4));
  Two2OneMux two2onemux_3 (.in_1(two2onemux_1_out_4), .S(S1), .B(two2onemux_2_out_4), .out_4(out_7));
endmodule
