// Logisim project Part45.circ as structural Verilog: 2 circuits, main circuit main
module main (
  input  [3:0] B,
  input  [15:0] A,
  output [15:0] Out1
);

  wire [15:0] multiplexer_1_out, multiplexer_2_out, multiplexer_3_out;

  Multiplexer #(.width(16), .enable("false")) multiplexer_1 (.in0(A), .in1(A), .out(multiplexer_1_out), .sel(B[3]));
  Multiplexer #(.width(16), .enable("false")) multiplexer_2 (
    .in0(multiplexer_1_out), .in1({multiplexer_1_out[3:0], multiplexer_1_out[15:4]}),
    .out(multiplexer_2_out), .sel(B[2]));
  Multiplexer #(.width(16), .enable("false")) multiplexer_3 (
    .in0(multiplexer_2_out), .in1({multiplexer_2_out[1:0], multiplexer_2_out[15:2]}),
    .out(multiplexer_3_out), .sel(B[1]));
  Multiplexer #(.width(16), .enable("false")) multiplexer_4 (
    .in0(multiplexer_3_out), .in1({multiplexer_3_out[0], multiplexer_3_out[15:1]}), .out(Out1), .sel(B[0]));

  // Notes on the sheet:
  //   rotr
endmodule

module Ex4 (
  input  [7:0] In1,
  output Out1,
  output [7:0] Out2
);

  and and_1 (Out1, In1[0], In1[7]);
  not not_1 (Out2[7], In1[7]);

  assign Out2[6:0] = In1[6:0];
endmodule
